// Logisim project Binary_multiplier.circ as structural Verilog: 3 circuits, main circuit main
module main (
  input  in_1,
  input  in_2,
  input  in_3,
  input  in_4,
  output out_5
);

  wire and_1_out, and_2_out, not_1_out, not_2_out, not_3_out, not_4_out;

  not not_1 (not_1_out, in_1);
  not not_2 (not_2_out, in_2);
  not not_3 (not_3_out, in_3);
  not not_4 (not_4_out, in_4);
  and and_1 (and_1_out, in_1, in_2, in_3, in_4);
  and and_2 (and_2_out, not_1_out, not_2_out, not_3_out, not_4_out);
  or or_1 (out_5, and_1_out, and_2_out);
endmodule

module binary_multip (
  input  a,
  input  b,
  input  c,
  input  d,
  output x,
  output y,
  output z,
  output u
);

  wire and_2_out, and_3_out, and_4_out, and_5_out, and_6_out, and_7_out, not_1_out, not_2_out, not_3_out,
       not_4_out, not_5_out, not_6_out;

  and and_1 (x, a, b, c, d);
  not not_1 (not_1_out, b);
  and and_2 (and_2_out, a, not_1_out, c);
  and and_3 (and_3_out, a, c, not_2_out);
  not not_2 (not_2_out, d);
  not not_3 (not_3_out, a);
  and and_4 (and_4_out, not_3_out, b, c);
  and and_5 (and_5_out, b, c, not_4_out);
  not not_4 (not_4_out, d);
  and and_6 (and_6_out, a, not_5_out, d);
  not not_5 (not_5_out, b);
  not not_6 (not_6_out, c);
  and and_7 (and_7_out, a, not_6_out, d);
  and and_8 (u, b, d);
  or or_1 (y, and_2_out, and_3_out);
  or or_2 (z, and_4_out, and_5_out, and_6_out, and_7_out);
endmodule

module comparator (
  input  A1,
  input  A0,
  input  B1,
  input  B0,
  output M,
  output E,
  output L
);

  wire and_1_out, and_2_out, and_3_out, and_4_out, and_5_out, and_6_out, and_7_out, and_8_out, and_9_out,
       and_10_out, not_1_out, not_2_out, not_3_out, not_4_out, not_5_out, not_6_out, not_7_out, not_8_out,
       not_9_out, not_10_out, not_11_out, not_12_out, not_13_out, not_14_out, not_15_out, not_16_out;

  not not_1 (not_1_out, B1);
  and and_1 (and_1_out, A0, not_1_out, not_2_out);
  not not_2 (not_2_out, B0);
  and and_2 (and_2_out, A1, not_3_out);
  not not_3 (not_3_out, B1);
  and and_3 (and_3_out, A1, A0, not_4_out);
  not not_4 (not_4_out, B0);
  not not_5 (not_5_out, A1);
  not not_6 (not_6_out, A0);
  not not_7 (not_7_out, B1);
  not not_8 (not_8_out, B0);
  not not_9 (not_9_out, A1);
  not not_10 (not_10_out, B1);
  not not_11 (not_11_out, A0);
  not not_12 (not_12_out, B0);
  not not_13 (not_13_out, A1);
  not not_14 (not_14_out, A0);
  and and_4 (and_4_out, not_13_out, not_14_out, B0);
  not not_15 (not_15_out, A1);
  and and_5 (and_5_out, not_15_out, B1);
  not not_16 (not_16_out, A0);
  and and_6 (and_6_out, not_16_out, B1, B0);
  or or_1 (M, and_1_out, and_2_out, and_3_out);
  and and_7 (and_7_out, not_5_out, not_6_out, not_7_out, not_8_out);
  and and_8 (and_8_out, not_9_out, A0, not_10_out, B0);
  and and_9 (and_9_out, A1, not_11_out, B1, not_12_out);
  and and_10 (and_10_out, A1, A0, B1, B0);
  or or_2 (L, and_4_out, and_5_out, and_6_out);
  or or_3 (E, and_7_out, and_8_out, and_9_out, and_10_out);
endmodule
