// Logisim project Memory.circ as structural Verilog
module _2_bit_binary_up_ripple_counter (
  input  in_1,
  output out_2,
  output out_3,
  output out_4,
  output out_5
);

  wire clock_1_out;

  Clock clock_1 (.out(clock_1_out));
  J_K_Flip_Flop #(.trigger("falling")) j_k_ff_1 (
    .J(1'b1), .clk(clock_1_out), .K(1'b1), .Q(out_3), .reset(in_1));  // open: Qn, preset, en
  T_Flip_Flop #(.trigger("falling")) t_ff_1 (
    .clk(clock_1_out), .T(1'b1), .Q(out_5), .reset(in_1));  // open: Qn, preset, en
  J_K_Flip_Flop #(.trigger("falling")) j_k_ff_2 (
    .J(1'b1), .clk(out_3), .K(1'b1), .Q(out_2), .reset(in_1));  // open: Qn, preset, en
  T_Flip_Flop #(.trigger("falling")) t_ff_2 (.clk(out_5), .T(1'b1), .Q(out_4), .reset(in_1));  // open: Qn, preset, en

  // Notes on the sheet:
  //   Q0
  //   Q1
endmodule

module _2_bit_binary_down_ripple_counter (
  input  in_1,
  output out_2,
  output out_3
);

  wire clock_1_out, j_k_ff_1_qn;

  Clock clock_1 (.out(clock_1_out));
  J_K_Flip_Flop #(.trigger("falling")) j_k_ff_1 (
    .J(1'b1), .clk(clock_1_out), .K(1'b1), .Q(out_3), .Qn(j_k_ff_1_qn), .reset(in_1));  // open: preset, en
  J_K_Flip_Flop #(.trigger("falling")) j_k_ff_2 (
    .J(1'b1), .clk(j_k_ff_1_qn), .K(1'b1), .Q(out_2), .reset(in_1));  // open: Qn, preset, en
endmodule

module _2_bit_binary_up_down_ripple_counter (
  input  up_ndown,
  input  in_2,
  output out_3,
  output out_4
);

  wire and_1_out, and_2_out, clock_1_out, j_k_ff_1_qn, not_1_out, or_1_out;

  not not_1 (not_1_out, up_ndown);
  Clock clock_1 (.out(clock_1_out));
  J_K_Flip_Flop #(.trigger("falling")) j_k_ff_1 (
    .J(1'b1), .clk(clock_1_out), .K(1'b1), .Q(out_4), .Qn(j_k_ff_1_qn), .reset(in_2));  // open: preset, en
  and and_1 (and_1_out, up_ndown, out_4);
  or or_1 (or_1_out, and_1_out, and_2_out);
  and and_2 (and_2_out, j_k_ff_1_qn, not_1_out);
  J_K_Flip_Flop #(.trigger("falling")) j_k_ff_2 (
    .J(1'b1), .clk(or_1_out), .K(1'b1), .Q(out_3), .reset(in_2));  // open: Qn, preset, en

  // Notes on the sheet:
  //   Q0
  //   Q1
endmodule

module _4_bit_up_down_ripple_counter (
  input  nup_down,
  input  in_2,
  output out_3,
  output out_4,
  output out_5,
  output out_6
);

  wire and_1_out, and_2_out, and_3_out, and_4_out, and_5_out, and_6_out, clock_1_out, n7_segment_driver_1_a,
       n7_segment_driver_1_b, n7_segment_driver_1_c, n7_segment_driver_1_d, n7_segment_driver_1_e,
       n7_segment_driver_1_f, n7_segment_driver_1_g, not_1_out, or_1_out, or_2_out, or_3_out, t_ff_1_qn,
       t_ff_2_qn, t_ff_3_qn;

  Clock clock_1 (.out(clock_1_out));
  not not_1 (not_1_out, nup_down);
  and and_1 (and_1_out, nup_down, out_6);
  T_Flip_Flop t_ff_1 (.clk(clock_1_out), .T(1'b1), .Q(out_6), .Qn(t_ff_1_qn), .reset(in_2));  // open: preset, en
  and and_2 (and_2_out, t_ff_1_qn, not_1_out);
  or or_1 (or_1_out, and_1_out, and_2_out);
  _7_segment_driver u_7_segment_driver_1 (
    .D0(out_3), .D1(out_4), .D2(out_5), .D4(out_6), .a(n7_segment_driver_1_a), .b(n7_segment_driver_1_b),
    .c(n7_segment_driver_1_c), .d(n7_segment_driver_1_d), .e(n7_segment_driver_1_e),
    .f(n7_segment_driver_1_f), .g(n7_segment_driver_1_g));
  T_Flip_Flop t_ff_2 (.clk(or_1_out), .T(1'b1), .Q(out_5), .Qn(t_ff_2_qn), .reset(in_2));  // open: preset, en
  _7_Segment_Display u_7_segment_display_1 (
    .g(n7_segment_driver_1_g), .f(n7_segment_driver_1_f), .a(n7_segment_driver_1_a),
    .b(n7_segment_driver_1_b), .e(n7_segment_driver_1_e), .d(n7_segment_driver_1_d), .c(n7_segment_driver_1_c));  // open: dp
  and and_3 (and_3_out, nup_down, out_5);
  or or_2 (or_2_out, and_3_out, and_4_out);
  and and_4 (and_4_out, t_ff_2_qn, not_1_out);
  T_Flip_Flop t_ff_3 (.clk(or_2_out), .T(1'b1), .Q(out_4), .Qn(t_ff_3_qn), .reset(in_2));  // open: preset, en
  and and_5 (and_5_out, nup_down, out_4);
  or or_3 (or_3_out, and_5_out, and_6_out);
  and and_6 (and_6_out, t_ff_3_qn, not_1_out);
  T_Flip_Flop t_ff_4 (.clk(or_3_out), .T(1'b1), .Q(out_3), .reset(in_2));  // open: Qn, preset, en

  // Other names for the same wires on the sheet: CLR = in_2; Q0 = out_6; Q1 = out_5; Q2 = out_4; Q3 = out_3
endmodule

module _7_segment_driver (
  input  D0,
  input  D1,
  input  D2,
  input  D4,
  output a,
  output b,
  output c,
  output d,
  output e,
  output f,
  output g
);

  wire and_1_out, and_2_out, and_3_out, and_4_out, and_5_out, and_6_out, and_7_out, and_8_out, and_9_out,
       and_10_out, and_11_out, and_12_out, and_13_out, and_14_out, and_15_out, and_16_out, and_17_out,
       and_18_out, and_19_out, and_20_out, and_21_out, and_22_out, and_23_out, not_1_out, not_2_out,
       not_3_out, not_4_out, not_5_out, not_6_out, not_7_out, not_8_out, not_9_out, not_10_out, not_11_out,
       not_12_out, not_13_out, not_14_out, not_15_out, not_16_out, not_17_out, not_18_out, not_19_out,
       not_20_out, not_21_out, not_22_out, not_23_out, not_24_out, not_25_out, not_26_out, not_27_out,
       not_28_out, not_29_out, not_30_out, not_31_out, not_32_out, not_33_out, not_34_out, not_35_out,
       not_36_out, not_37_out, not_38_out, not_39_out, not_40_out, not_41_out, not_42_out, not_43_out,
       not_44_out;

  not not_1 (not_1_out, D0);
  and and_1 (and_1_out, not_1_out, not_2_out, not_3_out);
  not not_2 (not_2_out, D1);
  not not_3 (not_3_out, D4);
  not not_4 (not_4_out, D0);
  and and_2 (and_2_out, not_4_out, D2);
  not not_5 (not_5_out, D0);
  and and_3 (and_3_out, not_5_out, D1, D4);
  not not_6 (not_6_out, D1);
  and and_4 (and_4_out, D0, not_6_out, not_7_out);
  not not_7 (not_7_out, D2);
  not not_8 (not_8_out, D0);
  and and_5 (and_5_out, not_8_out, not_9_out);
  not not_9 (not_9_out, D1);
  not not_10 (not_10_out, D1);
  and and_6 (and_6_out, not_10_out, not_11_out);
  not not_11 (not_11_out, D2);
  not not_12 (not_12_out, D0);
  and and_7 (and_7_out, not_12_out, D2, D4);
  not not_13 (not_13_out, D1);
  and and_8 (and_8_out, not_13_out, not_14_out);
  not not_14 (not_14_out, D2);
  not not_15 (not_15_out, D0);
  and and_9 (and_9_out, not_15_out, D4);
  not not_16 (not_16_out, D0);
  and and_10 (and_10_out, not_16_out, D1);
  not not_17 (not_17_out, D0);
  not not_18 (not_18_out, D1);
  not not_19 (not_19_out, D4);
  not not_20 (not_20_out, D0);
  not not_21 (not_21_out, D1);
  not not_22 (not_22_out, D0);
  not not_23 (not_23_out, D4);
  not not_24 (not_24_out, D0);
  not not_25 (not_25_out, D2);
  not not_26 (not_26_out, D1);
  not not_27 (not_27_out, D2);
  not not_28 (not_28_out, D1);
  and and_11 (and_11_out, not_28_out, not_29_out, not_30_out);
  not not_29 (not_29_out, D2);
  not not_30 (not_30_out, D4);
  not not_31 (not_31_out, D0);
  and and_12 (and_12_out, not_31_out, D2, not_32_out);
  not not_32 (not_32_out, D4);
  not not_33 (not_33_out, D0);
  not not_34 (not_34_out, D2);
  and and_13 (and_13_out, not_33_out, not_34_out, not_35_out);
  not not_35 (not_35_out, D4);
  not not_36 (not_36_out, D0);
  and and_14 (and_14_out, not_36_out, D1, not_37_out);
  not not_37 (not_37_out, D2);
  not not_38 (not_38_out, D0);
  and and_15 (and_15_out, not_38_out, D1, not_39_out);
  not not_39 (not_39_out, D4);
  not not_40 (not_40_out, D1);
  and and_16 (and_16_out, D0, not_40_out, not_41_out);
  not not_41 (not_41_out, D2);
  not not_42 (not_42_out, D0);
  and and_17 (and_17_out, not_42_out, D2, not_43_out);
  not not_43 (not_43_out, D4);
  not not_44 (not_44_out, D0);
  and and_18 (and_18_out, not_44_out, D1);
  or or_1 (a, and_1_out, and_2_out, and_3_out, and_4_out);
  or or_2 (b, and_5_out, and_6_out, and_7_out);
  or or_3 (c, and_8_out, and_9_out, and_10_out);
  and and_19 (and_19_out, not_17_out, not_18_out, not_19_out);
  and and_20 (and_20_out, not_20_out, not_21_out, D2);
  and and_21 (and_21_out, not_22_out, D2, not_23_out);
  and and_22 (and_22_out, not_24_out, D1, not_25_out, D4);
  and and_23 (and_23_out, D0, not_26_out, not_27_out);
  or or_4 (e, and_11_out, and_12_out);
  or or_5 (f, and_13_out, and_14_out, and_15_out, and_16_out);
  or or_6 (g, and_17_out, and_18_out);
  or or_7 (d, and_19_out, and_20_out, and_21_out, and_22_out, and_23_out);
  _7_Segment_Display u_7_segment_display_1 (.g(g), .f(f), .a(a), .b(b), .e(e), .d(d), .c(c));  // open: dp
endmodule
