// Logisim project adders and subtractors.circ as structural Verilog: 5 circuits, main circuit main
module main (
);

  _2_s_compelement u_2_s_compelement_1 ();  // open: in_1, in_7, in_2, in_8, in_3, in_9, in_4, in_10, in_5, in_11, in_6, in_12, out_13, out_14, out_15, out_16, out_17, out_18, out_19
  parallel_full_adder parallel_full_adder_1 ();  // open: in_1, in_7, in_2, in_8, in_3, in_9, in_4, in_10, in_5, in_11, in_6, in_12, out_13, out_14, out_15, out_16, out_17, out_18, out_19
endmodule

module _2_s_compelement (
  input  in_1,
  input  in_2,
  input  in_3,
  input  in_4,
  input  in_5,
  input  in_6,
  input  in_7,
  input  in_8,
  input  in_9,
  input  in_10,
  input  in_11,
  input  in_12,
  output out_13,
  output out_14,
  output out_15,
  output out_16,
  output out_17,
  output out_18,
  output out_19
);

  wire full_adder_2_cout, full_adder_3_cout, full_adder_4_cout, full_adder_5_cout, full_adder_6_cout,
       full_adder_7_cout, not_1_out, not_2_out, not_3_out, not_4_out, not_5_out, not_6_out;

  full_adder full_adder_1 (.A(1'b1), .B(1'b1), .Cin(full_adder_2_cout), .S(out_13));  // open: Cout
  not not_1 (not_1_out, in_8);
  not not_2 (not_2_out, in_7);
  full_adder full_adder_2 (.A(not_2_out), .B(in_1), .Cin(full_adder_3_cout), .S(out_14), .Cout(full_adder_2_cout));
  not not_3 (not_3_out, in_10);
  not not_4 (not_4_out, in_9);
  full_adder full_adder_3 (.A(not_1_out), .B(in_2), .Cin(full_adder_4_cout), .S(out_15), .Cout(full_adder_3_cout));
  not not_5 (not_5_out, in_11);
  full_adder full_adder_4 (.A(not_4_out), .B(in_3), .Cin(full_adder_5_cout), .S(out_16), .Cout(full_adder_4_cout));
  not not_6 (not_6_out, in_12);
  full_adder full_adder_5 (.A(not_3_out), .B(in_4), .Cin(full_adder_6_cout), .S(out_17), .Cout(full_adder_5_cout));
  full_adder full_adder_6 (.A(not_5_out), .B(in_5), .Cin(full_adder_7_cout), .S(out_18), .Cout(full_adder_6_cout));
  full_adder full_adder_7 (.A(not_6_out), .B(in_6), .Cin(1'b1), .S(out_19), .Cout(full_adder_7_cout));
endmodule

module parallel_full_adder (
  input  in_1,
  input  in_2,
  input  in_3,
  input  in_4,
  input  in_5,
  input  in_6,
  input  in_7,
  input  in_8,
  input  in_9,
  input  in_10,
  input  in_11,
  input  in_12,
  output out_13,
  output out_14,
  output out_15,
  output out_16,
  output out_17,
  output out_18,
  output out_19
);

  wire full_adder_2_cout, full_adder_3_cout, full_adder_4_cout, full_adder_5_cout, full_adder_6_cout,
       full_adder_7_cout;

  full_adder full_adder_1 (.A(1'b0), .B(1'b0), .Cin(full_adder_2_cout), .S(out_13));  // open: Cout
  full_adder full_adder_2 (.A(in_7), .B(in_1), .Cin(full_adder_3_cout), .S(out_14), .Cout(full_adder_2_cout));
  full_adder full_adder_3 (.A(in_8), .B(in_2), .Cin(full_adder_4_cout), .S(out_15), .Cout(full_adder_3_cout));
  full_adder full_adder_4 (.A(in_9), .B(in_3), .Cin(full_adder_5_cout), .S(out_16), .Cout(full_adder_4_cout));
  full_adder full_adder_5 (.A(in_10), .B(in_4), .Cin(full_adder_6_cout), .S(out_17), .Cout(full_adder_5_cout));
  full_adder full_adder_6 (.A(in_11), .B(in_5), .Cin(full_adder_7_cout), .S(out_18), .Cout(full_adder_6_cout));
  full_adder full_adder_7 (.A(in_12), .B(in_6), .Cin(1'b0), .S(out_19), .Cout(full_adder_7_cout));
endmodule

module full_adder (
  input  A,
  input  B,
  input  Cin,
  output S,
  output Cout
);

  wire and_1_out, and_2_out, xor_1_out;

  xor xor_1 (xor_1_out, A, B);
  and and_1 (and_1_out, B, A);
  xor xor_2 (S, xor_1_out, Cin);
  and and_2 (and_2_out, xor_1_out, Cin);
  or or_1 (Cout, and_2_out, and_1_out);
endmodule

module full_subtractor (
  input  Bin,
  input  B,
  input  A,
  output D,
  output Bout
);

  wire and_1_out, and_2_out, and_3_out, not_1_out, xor_1_out;

  not not_1 (not_1_out, A);
  and and_1 (and_1_out, not_1_out, Bin);
  and and_2 (and_2_out, not_1_out, B);
  and and_3 (and_3_out, B, Bin);
  xor xor_1 (xor_1_out, Bin, B);
  or or_1 (Bout, and_1_out, and_2_out, and_3_out);
  xor xor_2 (D, xor_1_out, A);

  // Notes on the sheet:
  //   ~A . Bin
  //   ~A . B
  //   B . Bin
endmodule
